# Fritzing sketch Assignment Circuit Diagram - K00237093 - IOT (saved by Fritzing 0.9.3b)
breadboards: 1

parts:
  PIR1 = PIR sensor
  Raspberry_Pi1 = Raspberry Pi B+
  J1 = Piezo Speaker
  S1 = Pushbutton [package="[THT]"]
  R1 = Resistor [tolerance=±5% resistance=220 package="2512 [SMD]"]
  LED1 = smd LED [color="Red (633nm)" package="1206 [SMD]"]
  PIR2 = PIR sensor

nets:
  VDD: PIR1.VDD, Raspberry_Pi1.5V, PIR2.VDD
  N1: PIR1.SIG, Raspberry_Pi1.GPIO20
  GND: PIR1.GND, Raspberry_Pi1.GPIO3, Raspberry_Pi1.GPIO27, Raspberry_Pi1.GND, J1.pin1, J1.pin2, S1.Pin_1, S1.Pin_2, LED1.cathode, PIR2.GND
  N2: Raspberry_Pi1.GPIO17, Raspberry_Pi1.GPIO18, R1.Pin_1
  N3: Raspberry_Pi1.GPIO26, PIR2.SIG
  N4: Raspberry_Pi1.GPIO16, S1.Pin_3, S1.Pin_4
  N5: R1.Pin_0, LED1.anode

notes:
  Camera to be fitted here in Camera Slot
